# Fritzing sketch layout (saved by Fritzing 0.9.6b)

parts:
  Mod1 = Raspberry Pi Pico
  OLED1 = OLED Mono 0.56 inch blue or white
  Part1 = Adafruit CP2102N Friend [part_number="Adafruit #5335"]
  U2 = mini DIN 6 Connector [package=mini-din6]

nets:
  N1: Mod1.pin_1, Part1.RXD
  N2: Mod1.pin_2, Part1.TXD
  GND: Mod1.pin_3, Mod1.pin_18, Mod1.pin_38, Mod1.pin_42, OLED1.GND, Part1.GND, U2.3
  N3: Mod1.pin_15, OLED1.VCC
  N4: Mod1.pin_16, OLED1.SDA
  N5: Mod1.pin_17, OLED1.SCL
  N6: Mod1.pin_21, U2.5
  N7: Mod1.pin_22, U2.1
  N8: Mod1.pin_36, U2.4

notes:
  VCC (3.3v)
  GND
  DATA
  CLK

custom parts:
  Raspberry Pi Pico: Raspberry Pi Pico. Based around the RP2040 microcontroller the Pico is a low cost microcontroller device bringing Raspberry Pi quality, cost, and easy of use to the microcontroller space. Jan 2021, Split part in to two versions: tht (this one) and SMD. This one will drill holes for a .1 in header in pcb to allow plugging in the module as well as providing pads to solder the module to the top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
  OLED Mono 0.56 inch blue or white: OLED, I2C 3.3V - 5V Blue and White text versions
  Adafruit CP2102N Friend: Long gone are the days of parallel ports and serial ports. Now the USB port reigns supreme! But USB is hard, and you just want to transfer your every-day serial data from a microcontroller to computer. What now? Enter the Adafruit CP2102N Friend! The CP2102N is very similar to the CP2104. Despite having a name with a lower number, its actually considered the successor/next generation to the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
  mini DIN 6 Connector: mini DIN 6 Connector Commonly found on the back of a computer for PS2 keyboard and mice. Schematic and footprint are proven. Spark Fun Electronics SKU : PRT-08509
